# Fritzing sketch FlowerIO_v.0.1 (saved by Fritzing 0.9.3b)

parts:
  Part1 = Arduino Uno (Rev3)
  VCC1_6V = 4 x AAA Battery Mount
  Temperature_sensor = Grove Temperature Sensor
  Soil_moisture_sensor = Soil Moisture Sensor
  HC-05_Bluetooth_Module = Bluetooth HC-05 Macho
  WATER_PUMP = DC Motor
  LED1 = LED - 5mm [color="Red (633nm)" package="5 mm [THT]"]
  R1 = Resistor [tolerance=±5% resistance=220 package=THT]
  DC_driver = IFR520 MOS module [package=THT]
  VCC2 = Battery block 9V
  or_L293D_for_DC_motor = L293D [package=THT]  # not connected
  on/off = Toggle Switch [package=THT]

nets:
  N1: Part1.A0, Soil_moisture_sensor.SIG
  N2: Part1.A1, Temperature_sensor.SIG
  N3: Part1.D9_PWM, DC_driver.SIG
  N4: Part1.D10_PWM/SS, HC-05_Bluetooth_Module.TXD
  N5: Part1.D11_PWM/MOSI, HC-05_Bluetooth_Module.RXD
  N6: Part1.D12/MISO, R1.Pin_1
  GND: Part1.GND, VCC1_6V.-, Temperature_sensor.GND, Soil_moisture_sensor.GND, HC-05_Bluetooth_Module.GND, LED1.cathode, DC_driver.GND, VCC2.-
  VCC: Part1.5V, Temperature_sensor.VCC, Soil_moisture_sensor.VCC, HC-05_Bluetooth_Module.VCC, DC_driver.VCC
  N7: Part1.VIN, on/off.L1
  N8: VCC1_6V.+, on/off.COM
  N9: WATER_PUMP.pin_1, DC_driver.V+
  N10: WATER_PUMP.pin_2, DC_driver.V-
  N11: DC_driver.VIN, VCC2.+

notes:
  L293D can also be used to control the DC motor.
  See this tutorial:
  https://lastminuteengineers.com/l293d-dc-motor-arduino-tutorial/
